# Fritzing sketch layout (saved by Fritzing 0.9.3b)

parts:
  Part1 = Arduino Uno (Rev3)
  LED1 = 7-SEGMENT-4DIGIT-YOUNGSUN [package=7-segment-4digit-youngsun-longpads]
  S1 = Pushbutton [package="[SMD]"]
  R1 = Resistor [tolerance=±5% resistance=10k package=THT]
  Part3 = HX711 Weighing Sensor Module
  S2 = Pushbutton [package="[SMD]"]
  R2 = Resistor [tolerance=±5% resistance=10k package=THT]
  VCC1 = 4 x AAA Battery Mount

nets:
  N1: Part1.A4/SDA, LED1.DAT
  N2: Part1.A5/SCL, LED1.CLK
  N3: Part1.D8, S1.Pin_3, S1.Pin_4, R1.Pin_0
  N4: Part1.D9_PWM, S2.Pin_3, S2.Pin_4, R2.Pin_0
  N5: Part1.D2, Part3.CK/TX
  N6: Part1.D3_PWM, Part3.DO/RX
  N7: Part1.5V, LED1.+
  N8: Part1.GND, LED1.-, VCC1.-
  N9: Part1.VIN, VCC1.+

notes:
  it's not the correct HX711 schema but it's the only one available online
  to load cell
  this button will not really power on/off the board but just turn on/off the display software side
  tare
  10kΩ
  power
  the final design should have the power button here to really power on/off the board
  not part of the board

custom parts:
  7-SEGMENT-4DIGIT-YOUNGSUN: This is a part for the 4-Digit 7-segment LEDs from Young Sun. Different from the Digikey LEDs, all 16 pins are used. The LONGPADS Variant is used for a test jig, but you may like it because there is more pad to solder to. If you are concerned about routing space, the standard works just fine though.
